# Fritzing sketch Nano_Nrf95w_V2 (saved by Fritzing 0.9.3b)
circuit board: 7.1cm x 2.11101cm
breadboards: 1

parts:
  Ant = SMA Antenna Connector [package=sma-edge]
  RFM95W = RFM9xW
  74HC4050 = 74HC4050 [package=so16]
  Nano = Arduino Nano (Rev3.0)

nets:
  GND: Ant.GND, RFM95W.GND, 74HC4050.GND, Nano.GND
  N1: Ant.SIGNAL, RFM95W.ANT
  N2: RFM95W.MISO, Nano.D12/MISO
  N3: RFM95W.MOSI, 74HC4050.6Y
  N4: RFM95W.SCK, 74HC4050.2Y
  N5: RFM95W.NSS, 74HC4050.5Y
  N6: RFM95W.RESET, Nano.RESET
  VCC: RFM95W.VCC, 74HC4050.VCC, Nano.3V3
  N7: RFM95W.DIO0, Nano.D7
  N8: RFM95W.DIO1, Nano.D8
  N9: RFM95W.DIO2, Nano.D9
  N10: 74HC4050.2A, Nano.D13/SCK
  N11: 74HC4050.5A, Nano.D10
  N12: 74HC4050.6A, Nano.D11/MOSI

custom parts:
  RFM9xW: RFM9xW Module connector
  74HC4050: Hex non-inverting HIGH-to-LOW level shifter
